# Fritzing sketch Sweeper with Leds (saved by Fritzing 1.0.1rc)
breadboards: 2

parts:
  LED1 = LED - 5mm [color="Red (633nm)" current=0.030A package="5 mm [THT]"]
  LED2 = LED - 5mm [color="Yellow (595nm)" current=0.030A package="5 mm [THT]"]
  LED3 = LED - 5mm [color="Green (555nm)" current=0.030A package="5 mm [THT]"]
  R1 = Resistor [tolerance=±5% resistance=220 package="1206 [SMD]"]
  R2 = Resistor [tolerance=±5% resistance=220 package="1206 [SMD]"]
  R3 = Resistor [tolerance=±5% resistance=220 package="1206 [SMD]"]
  J1 = Basic Servo
  J2 = Basic Servo
  U2 = ESP8266 NodeMCU LoLin module

nets:
  GND: LED1.cathode, LED2.cathode, LED3.cathode, J1.gnd, J2.gnd, U2.GND
  N1: LED1.anode, R1.Pin_1
  N2: LED2.anode, R2.Pin_1
  N3: LED3.anode, R3.Pin_1
  VCC: J1.vcc, J2.vcc, U2.3V3

custom parts:
  ESP8266 NodeMCU LoLin module: ESP8266 based NodeMCU

// code stored in the sketch: Sweeper with Leds.ino
#include<Servo.h>

class LedMachine {
  int ledPin;
  long timeOn;
  long timeOff;
  String label;
  
  int ledState;
  unsigned long previousMillis;
  
public:
  LedMachine(int pin, long t_on, long t_off, String name) {
    this->ledPin        = pin;
    this->timeOn        = t_on;
    this->timeOff       = t_off;
    this->ledState      = LOW;
    this->previousMillis = 0;
    this->label          = name;
    
    pinMode(ledPin, OUTPUT);
  }

  void Update() {
    /// Doc: https://www.arduino.cc/reference/pt/language/functions/time/millis/
    unsigned long currentMillis = millis();

    if((this->ledState == HIGH) && ((currentMillis - this->previousMillis) >= this->timeOn)) {
      this->ledState = LOW; 
      this->previousMillis = currentMillis;
      digitalWrite(this->ledPin, this->ledState);
    }
    else if((this->ledState == LOW) && ((currentMillis - this->previousMillis) >= this->timeOff)) {
      this->ledState = HIGH;
      this->previousMillis = currentMillis;
      digitalWrite(this->ledPin, this->ledState);
    }
  }
};

class Sweeper {
  Servo servo;
  int currentPosition;
  int increment;
  int updateInterval;
  unsigned long lastUpdate;

public:
  Sweeper(int interval) {
    this->updateInterval = interval;
    increment = 1;
  }

  void Attach(int pin) { this->servo.attach(pin); }
  void Detach() { this->servo.detach(); }

  void Update() {
    unsigned long currentMillis = millis();

    if((currentMillis - this->lastUpdate) > updateInterval) {
      this->lastUpdate = currentMillis;
      this->currentPosition += increment;
      this->servo.write(this->currentPosition);

      if((this->currentPosition >= 180) || (this->currentPosition <= 0)) this->increment = -this->increment;
    }
  }
};


LedMachine ledRed(8, 100, 400, "Vermelho");
LedMachine ledYellow(7, 350, 350, "Amarelo");
LedMachine ledGreen(6, 700, 300, "Verde");

Sweeper sweeper1(3);
Sweeper sweeper2(4);

  

void setup() {
  Serial.begin(11520);
  pinMode(LED_BUILTIN, OUTPUT);
  sweeper1.Attach(10);
  sweeper2.Attach(9);
}

void loop() {
  ledRed.Update();
  ledYellow.Update();
  ledGreen.Update();

  sweeper1.Update();
  sweeper2.Update();
}
